# Fritzing sketch Trinket_Neopixel_Ring (saved by Fritzing 0.9.3b)

parts:
  Part1 = NeoPixel Jewel
  U1 = LIPO-110mAh [package=lipo-110]
  Part2 = Adafruit Trinket 5V

nets:
  N1: Part1.Data_In, Part2.#0
  N2: Part1.VDD, U1.+, Part2.VBAT
  GND: Part1.GND, U1.-, Part2.GND

custom parts:
  NeoPixel Jewel: Seven of our the tiny 5050 (5mm x 5mm) smart RGB LEDs onto a beautiful, round PCB with mounting holes and a chainable design to create what we think is our most elegant (and evening-wear appropriate) NeoPixel board yet.
  Adafruit Trinket 5V: Trinket may be small, but do not be fooled by its size! It's a tiny microcontroller board, built around the Atmel ATtiny85, a little chip with a lot of power. We wanted to design a microcontroller board that was small enough to fit into any project, and low cost enough to use without hesitation. Perfect for when you don't want to give up your expensive dev-board and you aren't willing to take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
